// Logisim project cpu.circ as structural Verilog: 4 circuits, main circuit main
module main (
  input  [15:0] From_Instr_Mem,
  input  clk,
  output [15:0] r0,
  output [15:0] r1,
  output [15:0] r2,
  output [15:0] r3,
  output [15:0] Display_0,
  output [15:0] Display_1,
  output [15:0] Data_Mem_Data,
  output [15:0] Data_Mem_Addr,
  output [15:0] To_Instr_Mem,
  output Data_Mem_Write
);

  wire instruction_decode_1_regdest, main_1_p9, undriven;
  wire [1:0] instruction_decode_1_out_3, instruction_decode_1_out_4, instruction_decode_1_out_5,
       multiplexer_1_out;
  wire [15:0] data_memory_1_dataout, main_1_p10, main_1_p11, main_2_p2, multiplexer_2_out, WriteData;

  Instruction_Decode instruction_decode_1 (
    .RegDest(instruction_decode_1_regdest), .out_3(instruction_decode_1_out_3),
    .out_4(instruction_decode_1_out_4), .out_5(instruction_decode_1_out_5));  // open: in_1
  Multiplexer #(.width(2), .enable("false")) multiplexer_1 (
    .in0(instruction_decode_1_out_4), .in1(instruction_decode_1_out_5), .out(multiplexer_1_out),
    .sel(instruction_decode_1_regdest));
  // Regfile_main main_1: pin names not known; wires that end beside it: multiplexer_1_out, instruction_decode_1_out_5, instruction_decode_1_out_3, WriteData, r0, r1, r2, r3, main_1_p9, main_1_p10, main_1_p11
  Multiplexer #(.width(16), .enable("false")) multiplexer_2 (
    .in0(main_1_p10), .out(multiplexer_2_out));  // open: in1, sel
  Multiplexer #(.width(16), .enable("false")) multiplexer_3 (
    .in0(data_memory_1_dataout), .in1(main_2_p2), .out(WriteData), .sel(undriven));
  // alu_main main_2: pin names not known; wires that end beside it: multiplexer_2_out, main_2_p2
  Data_Memory data_memory_1 (
    .DataIn(main_2_p2), .Address(main_1_p11), .DataOut(data_memory_1_dataout), .MemWrite(Data_Mem_Write));  // open: Reset

  // Other names for the same wires on the sheet: d0[15:0] = Display_0; d1[15:0] = Display_1;
  //   MemWrite = Data_Mem_Write

  // Notes on the sheet:
  //   This is the current PC that you need to send as OUTPUT
  //   This is the instruction that you would receive as INPUT
  //   RegDest
  //   rd
  //   rt
  //   rs
  //   This is a CLK that is an INPUT driven from the harness.
  //   Remember, this circuit is loaded from the harness to be tested!
  //   DO NOT CHANGE THE LOCATIONS OF THE INPUTS OR OUTPUTS! IF YOU DO SO, YOU NEED TO MAKE SURE THE PINS ARE IN THE RIGHT PLACES!
  //   These are OUTPUTS of the circuit
  //   These are OUTPUTS of the circuit
endmodule

module Data_Memory (
  input  [15:0] DataIn,
  input  [15:0] Address,
  input  Reset,
  input  MemWrite,
  output [15:0] DataOut
);

  wire clk_out, not_1_out;

  Clock clk (.out(clk_out));
  assign DataOut = MemWrite ? DataIn : 16'bz;  // Controlled_Buffer controlled_buffer_1
  RAM #(.addrWidth(16), .dataWidth(16)) ram_1 (
    .addr(Address), .data(DataOut), .sel(1'b1), .clk(clk_out), .ld(not_1_out), .clr(Reset));
  not not_1 (not_1_out, MemWrite);
endmodule

module Instruction_Decode (
  input  [15:0] in_1,
  output RegDest,
  output [1:0] out_3,
  output [1:0] out_4,
  output [1:0] out_5
);

  wire [3:0] bitselector_1_out;
  wire [15:0] demultiplexer_1_out0;

  BitSelector #(.width(16), .group(4)) bitselector_1 (.in(in_1), .out(bitselector_1_out), .sel(2'b11));
  Demultiplexer #(.select(4), .width(16), .enable("false")) demultiplexer_1 (
    .out0(demultiplexer_1_out0), .in(in_1), .sel(bitselector_1_out));  // open: out1, out2, out3, out4, out5, out6, out7, out8, out9, out10, out11, out12, out13, out14, out15
  BitSelector #(.width(16)) bitselector_2 (.in(demultiplexer_1_out0), .out(RegDest), .sel(4'b0000));

  // Other names for the same wires on the sheet: rd[1:0] = out_4; rs[1:0] = out_3; rt[1:0] = out_5
endmodule

module R_type_Instruction_Decode (
  input  [15:0] in_1
);

  wire bitselector_2_out;
  wire [4:0] bitselector_1_out;

  BitSelector #(.width(16), .group(5)) bitselector_1 (.in(in_1), .out(bitselector_1_out), .sel(2'b00));
  BitSelector #(.width(5)) bitselector_2 (.in(bitselector_1_out), .out(bitselector_2_out), .sel(3'b111));

  // Notes on the sheet:
  //   select funct code
endmodule
